# Fritzing sketch scheme_lab2 (saved by Fritzing 0.9.3b)

parts:
  WeMos_D1_Mini1 = WeMos D1 Mini
  LED1 = LED - 3mm [color="Green (570nm)" package="3 mm [THT]"]
  LED2 = LED - 3mm [color="Yellow (592nm)" package="3 mm [THT]"]
  LED3 = LED - 3mm [color="Red (635nm)" package="3 mm [THT]"]
  R1 = Resistor [tolerance=±5% resistance=220 package="0805 [SMD]"]
  R2 = Resistor [tolerance=±5% resistance=220 package="0805 [SMD]"]
  R3 = Resistor [tolerance=±5% resistance=220 package="0805 [SMD]"]
  S2 = Pushbutton [package="[SMD]"]
  WeMos_D1_Mini2 = WeMos D1 Mini
  LED4 = LED - 3mm [color="Red (635nm)" package="3 mm [THT]"]
  LED5 = LED - 3mm [color="Yellow (592nm)" package="3 mm [THT]"]
  LED6 = LED - 3mm [color="Green (570nm)" package="3 mm [THT]"]
  R4 = Resistor [tolerance=±5% resistance=220 package="0805 [SMD]"]
  R5 = Resistor [tolerance=±5% resistance=220 package="0805 [SMD]"]
  R6 = Resistor [tolerance=±5% resistance=220 package="0805 [SMD]"]
  S3 = Pushbutton [package="[SMD]"]
  R7 = Resistor [tolerance=±5% resistance=220 package="0805 [SMD]"]

nets:
  5V: WeMos_D1_Mini1.5V, WeMos_D1_Mini2.5V
  N1: WeMos_D1_Mini1.D4, R3.Pin_1
  N2: WeMos_D1_Mini1.D5, R1.Pin_0
  N3: WeMos_D1_Mini1.D6, S2.Pin_1, S2.Pin_2
  N4: WeMos_D1_Mini1.D7, R2.Pin_0
  GND: WeMos_D1_Mini1.G, S2.Pin_4, WeMos_D1_Mini2.G, R7.Pin_1
  N5: WeMos_D1_Mini1.RX, WeMos_D1_Mini2.TX
  N6: WeMos_D1_Mini1.TX, WeMos_D1_Mini2.RX
  N7: LED1.anode, R2.Pin_1
  N8: LED2.anode, R1.Pin_1
  N9: LED3.anode, R3.Pin_0
  N10: WeMos_D1_Mini2.3V3, S3.Pin_3, S3.Pin_4, R7.Pin_0
  N11: WeMos_D1_Mini2.D3, R4.Pin_1
  N12: WeMos_D1_Mini2.D4, R6.Pin_0
  N13: WeMos_D1_Mini2.D7, R5.Pin_0
  N14: WeMos_D1_Mini2.D8, S3.Pin_2
  N15: LED4.anode, R4.Pin_0
  N16: LED5.anode, R6.Pin_1
  N17: LED6.anode, R5.Pin_1
